# Fritzing sketch 指纹识别锁 (saved by Fritzing 0.9.2b)
stripboards: 1

parts:
  元件1 = Arduino Uno (Rev3)
  VCC4 = Battery
  VCC3 = Battery
  LCD2 = LCD screen
  LCM1602_IIC2 = LCM1602 IIC [part_number="LCM1602 IIC" chip_label="LCM1602 IIC" package="DIP (Dual Inline) [THT]"]
  U1 = SWITCH_SPDT [package=kps-1290]
  J1 = Basic Servo
  DS3231 = DS3231
  AS608 = AS608

nets:
  N1: 元件1.A4/SDA, LCM1602_IIC2.SDA, DS3231.SDA
  N2: 元件1.A5/SCL, LCM1602_IIC2.SCL, DS3231.SCL
  N3: 元件1.D8, J1.pulse
  GND: 元件1.GND, VCC4.-, LCM1602_IIC2.GND, J1.gnd, DS3231.GND, AS608.GND
  N4: 元件1.D2, AS608.RX
  N5: 元件1.D3_PWM, AS608.TX
  3V3: 元件1.3V3, AS608.VIN
  VCC: 元件1.5V, LCM1602_IIC2.VCC, J1.vcc, DS3231.VCC
  N6: 元件1.VIN, U1.S
  N7: VCC4.+, VCC3.-
  N8: VCC3.+, U1.P
  VSS: LCD2.VSS, LCM1602_IIC2.VSS
  VDD: LCD2.VDD, LCM1602_IIC2.VDD
  N9: LCD2.V0, LCM1602_IIC2.V0
  N10: LCD2.RS, LCM1602_IIC2.RS
  N11: LCD2.R/W, LCM1602_IIC2.RW
  N12: LCD2.E, LCM1602_IIC2.E
  N13: LCD2.DB0, LCM1602_IIC2.D0
  N14: LCD2.DB1, LCM1602_IIC2.D1
  N15: LCD2.DB2, LCM1602_IIC2.D2
  N16: LCD2.DB3, LCM1602_IIC2.D3
  N17: LCD2.DB4, LCM1602_IIC2.D4
  N18: LCD2.DB5, LCM1602_IIC2.D5
  N19: LCD2.DB6, LCM1602_IIC2.D6
  N20: LCD2.DB7, LCM1602_IIC2.D7
  N21: LCD2.LED+, LCM1602_IIC2.A
  N22: LCD2.LED-, LCM1602_IIC2.K
  N23: LCM1602_IIC2.LED_A, LCM1602_IIC2.LED_B

notes:
  AS608 光学指纹识别模块
  舵机
  DS3231时间模块
  电源 6V - V9
  I2C LCD1602 模组
  Arduino UNO
  小型面包板

custom parts:
  LCM1602 IIC: I2C-Module to use a 1602 or 2004 LCD on with the wire.h libory Serial LCD Modul
  DS3231: DS3231 time
  AS608: AS608 fingerprint identification

// code stored in the sketch: Fingerprint_identification_lock.ino
//*********************************************************
//                指纹识别锁程序
//    作者：666小奇
//    硬件：Arduino  AS608指纹识别模块
//    提示：AS608与FPM10A程序兼容
//    说明：本程序未经作者允许禁止转载
//     QQ :1792498113
//    E-mil:liujiaqi7998@qq.com
//    接线：A4-SDA  A5-SCL  指纹识别模块接PIN2,PIN3详见下面介绍
//         蜂鸣器-PIN 9  舵机-PIN 8  自动休眠(可选)PIN -7
//    项目使用了 11492 字节，占用了 (35%) 程序存储空间。
//    全局变量使用了860字节，(41%)的动态内存
//    余留1188字节局部变量。最大为2048字节。
//**********************************************************


//引用库声明************************************************
#include <Adafruit_Fingerprint.h>  //指纹识别模块库
#include <SoftwareSerial.h>  //软串口通讯库
#include <Wire.h>  //I2C总线库
#include <LiquidCrystal_I2C.h>  //I2C1062屏幕库
#include <pt.h>  //多线程库
#include <DS3231.h>
//**********************************************************

//1602液晶自定义符号*************************************************
byte lcda[8] = {   0x08, 0x0f, 0x12, 0x0f, 0x0a, 0x1f, 0x02, 0x02,}; //年
byte lcdb[8] = {   0x0f, 0x09, 0x0f, 0x09, 0x0f, 0x09, 0x13, 0x01,}; //月
byte lcdc[8] = {   0x0f, 0x09, 0x09, 0x0f, 0x09, 0x09, 0x0f, 0x00,}; //日
byte lcdd[8] = {   0x18, 0x18, 0x07, 0x08, 0x08, 0x08, 0x07, 0x00,}; //°C
byte lcde[8] = {   0x04, 0x04, 0x0a, 0x15, 0x04, 0x04, 0x14, 0x0c,}; //小
byte lcdf[8] = {   0x04, 0x1f, 0x04, 0x0a, 0x1f, 0x1a, 0x1a, 0x0e,}; //奇
//*******************************************************************


//初始化时间模块*****************************************************
DS3231 Clock;
bool Century = false;
bool h12;
bool PM;
byte ADay, AHour, AMinute, ASecond, ABits;
bool ADy, A12h, Apm;
int year, month, date, DoW, week , hour, minute, second, temperature;
char dis1[16] = {0}, dis2[16] = {0};
//*****************************************************************


//指纹识别初始化********************************************
int getFingerprintIDez();
// pin #2 is IN from sensor (GREEN wire)  指纹传感器输入
// pin #3 is OUT from arduino  (WHITE wire)  指纹传感器输出
SoftwareSerial mySerial(2, 3);
Adafruit_Fingerprint finger = Adafruit_Fingerprint(&mySerial);
// On Leonardo/Micro or others with hardware serial, use those! #0 is green wire, #1 is white
//Adafruit_Fingerprint finger = Adafruit_Fingerprint(&Serial1);

//***********************************************************


//1062初始化*************************************************
LiquidCrystal_I2C lcd(0x3F, 16, 2);
// 设置为16个字符，2行LCD显示，地址0x27
//如果1062无显示那么注意地址设置
//***********************************************************


//舵机设置***************************************************
int servopin = 8  ; //设置舵机接口10
void servopulse(int angle)//定义一个脉冲函数
{
  int pulsewidth = (angle * 11) + 500; //将角度转化为500-2480的脉宽值
  digitalWrite(servopin, HIGH);   //将舵机接口电平至高
  delayMicroseconds(pulsewidth);  //延时脉宽值的微秒数
  digitalWrite(servopin, LOW);    //将舵机接口电平至低
  delayMicroseconds(20000 - pulsewidth);
}
//***********************************************************


//简单配置**************************************************
int Rtime = 0 ;//错误次数延时
static int counter1 , counter2 , counter3 ; //counter为定时计数器
//**********************************************************


//线程1，回到主页面状态舵机复位******************************
static int protothread1(struct pt *pt)

{
  PT_BEGIN(pt);  //线程开始
  while (1) //每个线程都不会死
  {
    PT_WAIT_UNTIL(pt, counter1 == 35 );
    //如果时间满了3.5秒左右，则继续执行，否则记录运行点，退出线程1
    counter1 = 0; //计数器置零
    for (int i = 0; i < 80; i++) //发送50个脉冲
    {
      servopulse(90);   //引用脉冲函数
    }
    lcdplay();
  }
  PT_END(pt); //线程结束
}
//线程2，错误重试等待时间清0*********************************
static int protothread2(struct pt *pt) //线程2，控制灯2
{
  PT_BEGIN(pt); //线程开始
  while (1) {   //每个线程都不会死
    PT_WAIT_UNTIL(pt, counter2 == 150);
    Rtime = 0 ;
    counter2 = 0; //计数清零
  }
  PT_END(pt);  //线程结束
}
//线程2，长时间无操作提示（pin7 低电平）可用作自动关机*********
static int protothread3(struct pt *pt) //线程2，控制灯2
{
  PT_BEGIN(pt); //线程开始
  while (1) {   //每个线程都不会死
    PT_WAIT_UNTIL(pt, counter3 == 200);
    digitalWrite(7, LOW);
  }
  PT_END(pt);  //线程结束
}
//*************************************************************


//lcd1602创建特殊字符（中文）**********************************
void diy()
{
  lcd.createChar(0, lcda);
  lcd.createChar(1, lcdb);
  lcd.createChar(2, lcdc);
  lcd.createChar(3, lcdd);
  lcd.createChar(4, lcde);
  lcd.createChar(5, lcdf);
}
//**************************************************************


//读取DS3231 参数**********************************************
void ReadDS3231()
{
  Wire.begin();
  second = Clock.getSecond();
  minute = Clock.getMinute();
  hour = Clock.getHour(h12, PM);
  week = Clock.getDoW();
  date = Clock.getDate();
  month = Clock.getMonth(Century);
  year = Clock.getYear();
  temperature = Clock.getTemperature();
}
void get_dis()          //1602液晶上每一位上显示的数据
{
  ReadDS3231();
  dis1[0] = '2';
  dis1[1] = '0';
  dis1[2] = 0x30 + year / 10;
  dis1[3] = 0x30 + year % 10;
  dis1[4] = 0;
  dis1[5] = 0x30 + month / 10;
  dis1[6] = 0x30 + month % 10;
  dis1[7] = 1;
  dis1[8] = 0x30 + date / 10;
  dis1[9] = 0x30 + date % 10;
  dis1[10] = 2;
  dis1[11] = ' ';
  dis1[12] = ' ';
  switch (week)
  {
    case 1: {
        dis1[13] = 'M';
        dis1[14] = 'o';
        dis1[15] = 'n';
      }
      break;
    case 2: {
        dis1[13] = 'T';
        dis1[14] = 'u';
        dis1[15] = 'e';
      }
      break;
    case 3: {
        dis1[13] = 'W';
        dis1[14] = 'e';
        dis1[15] = 'd';
      }
      break;
    case 4: {
        dis1[13] = 'T';
        dis1[14] = 'h';
        dis1[15] = 'u';
      }
      break;
    case 5: {
        dis1[13] = 'F';
        dis1[14] = 'r';
        dis1[15] = 'i';
      }
      break;
    case 6: {
        dis1[13] = 'S';
        dis1[14] = 'a';
        dis1[15] = 't';
      }
      break;
    case 7: {
        dis1[13] = 'S';
        dis1[14] = 'u';
        dis1[15] = 'n';
      }
      break;
  }
  dis2[0] = ' ';
  dis2[1] = 0x30 + hour / 10;
  dis2[2] = 0x30 + hour % 10;
  dis2[3] = ':';
  dis2[4] = 0x30 + minute / 10;
  dis2[5] = 0x30 + minute % 10;
  dis2[6] = ':';
  dis2[7] = 0x30 + second / 10;
  dis2[8] = 0x30 + second % 10;
  dis2[9] = ' ';
  dis2[10] = ' ';
  dis2[11] = 0x30 + temperature / 10;
  dis2[12] = 0x30 + temperature % 10;
  dis2[13] = '.';
  dis2[14] = 0x30 + 0;
  dis2[15] = 3;
}
//***********************************************************


//1602显示完整时间*******************************************
void lcdplay()
{
  get_dis();
  int k;
  lcd.setCursor( 0, 0);
  for (k = 0; k < 16; k++)
    lcd.write(dis1[k]);
  lcd.setCursor( 0, 1);
  for (k = 0; k < 16; k++)
    lcd.write(dis2[k]);
}
//**********************************************************


//***********************************************************
//程序初始化*************************************************
static struct pt pt1, pt2, pt3;
void setup()   {
  pinMode(7, OUTPUT); //设定舵机接口为输出接口
  digitalWrite(7, HIGH);
  tone(9, 700, 100);//蜂鸣器提示
  // 设置串行端口的数据速率
  Serial.begin(9600);
  // 设置指纹传感器串行端口的数据速率
  finger.begin(9600);
  // LCD初始化
  lcd.init(); // initialize the lcd
  lcd.backlight(); //Open the backlight
  //舵机初始化
  pinMode(servopin, OUTPUT); //设定舵机接口为输出接口
  //指纹传感器检查
  if (finger.verifyPassword()) {

    lcd.setCursor(0, 0);
    lcd.print("Found fingerprint sensor!"); //发现指纹传感器
  } else {

    lcd.setCursor(0, 0);
    lcd.print("Did not find fingerprint sensor :(");  //没有发现指纹传感器
    lcd.setCursor(0, 1);
    lcd.print("Check and Rest !");
    tone(9, 700, 100);//蜂鸣器提示
    delay(1000);
    tone(9, 700, 100);//蜂鸣器提示
    delay(3000);
    digitalWrite(7, LOW);
    while (1);
  }
  diy();
  //下面开始1602欢迎页面
  lcd.clear();
  lcd.setCursor(0, 0);
  lcd.print("Welcome to use");
  lcd.setCursor(0, 1);
  lcd.print("BY 666 ");
  lcd.write(4);
  lcd.print(" ");
  lcd.write(5);
  //下面开始线程初始化
  PT_INIT(&pt1);  //线程1初始化
  PT_INIT(&pt2);  //线程2初始化
  PT_INIT(&pt3);  //线程2初始化
  //下面舵机复位
  for (int i = 0; i < 50; i++) //发送50个脉冲
  {
    servopulse(90);   //引用脉冲函数
  }

  tone(9, 700, 100); //蜂鸣器提示完成
}


void loop() {
  protothread1(&pt1);  //执行线程1
  protothread1(&pt2);  //执行线程2
  protothread1(&pt3);  //执行线程2
  getFingerprintIDez() ; //读取指纹
  delay(10); //时间片，每片1秒，可根据具体应用设置大小
  //下面为计时器
  counter1++;
  counter2++;
  counter3++;
}


int getFingerprintIDez() {

  uint8_t p = finger.getImage();
  if (p != FINGERPRINT_OK) {
    return -1;
  } else { //读取成功
    tone(9, 900, 300); //蜂鸣器提示
    counter3 = 0 ; //计时器清0
    counter1 = 0 ;
  }

  p = finger.image2Tz();
  if (p != FINGERPRINT_OK)  return -1;

  p = finger.fingerFastSearch();
  if (p != FINGERPRINT_OK)
  { wrong();  //指纹错误
    return -1; //返回
  }
  int m ;
  m = finger.fingerID ; //得到指纹序号
  if (m != -1) {
    for (int i = 0; i < 50; i++) //发送50个脉冲，舵机解锁
    {
      servopulse(0);   //引用脉冲函数
    }
    tone(9, 1500, 300);//蜂鸣器提示
    //下面为1602提示
    lcd.clear();
    lcd.setCursor(0, 0);
    lcd.print("PASS");
    lcd.setCursor(0, 1);
    lcd.print("Found ID #"); lcd.print(m);
    Rtime = 0 ; //清除错误等待时间
  }
  return m; //返回
}


void wrong() {  //指纹错误
  tone(9, 500, 300); //蜂鸣器提示
  Rtime = Rtime + 1000 ; //计算错误等待时间
  //下面为1602显示
  lcd.clear();
  lcd.setCursor(0, 0);
  lcd.print("WRONG");
  lcd.setCursor(0, 1);
  lcd.print("Wait: "); lcd.print(Rtime / 1000); lcd.print(" s");
  counter2 = 0 ;//计时器复位
  delay(Rtime);  //等待时间
}
